# Fritzing sketch Display System (saved by Fritzing 0.9.10b)
breadboards: 2

parts:
  Part1 = Arduino Uno (Rev3)
  LED = smd LED [color="Red (633nm)" package="0805 [SMD]"]
  BUZZER/ALARM = Piezo Speaker
  ACCELEROMETER = GY-521 (MPU-6050) [form="♀ (female)" package=THT]
  ULTRASONIC_SENSOR = HC-SR04 Ultrasonic Distance Sensor
  SERVO_MOTOR = Dagu DGServo 9g (Pan and tilt) [part_number=RS001B]
  POTENTIOMETER = POT [knob_status=50% power=0.5W package=pot_mammoth]
  LCD_1 = LCD screen 16x2 IIC [part_number=101290]
  LASER_DIODE_3 = Electrolytic Capacitor [capacitance=1µF voltage=35V package="100 mil [THT, electrolytic]"]
  LASER_DIODE1 = Electrolytic Capacitor [capacitance=1µF voltage=35V package="100 mil [THT, electrolytic]"]
  LASER_DIODE_2 = Electrolytic Capacitor [capacitance=1µF voltage=35V package="100 mil [THT, electrolytic]"]
  LCD_2 = LCD screen 16x2 IIC [part_number=101290]  # not connected

nets:
  N1: Part1.A0, POTENTIOMETER.A
  N2: Part1.A4/SDA, ACCELEROMETER.pin4, ACCELEROMETER.pin5, LCD_1.SCL
  N3: Part1.A5/SCL, ACCELEROMETER.pin3, LCD_1.SDA
  GND: Part1.D8, Part1.GND, LED.cathode, LED.anode, BUZZER/ALARM.pin1, ACCELEROMETER.pin2, ULTRASONIC_SENSOR.GND, SERVO_MOTOR.gnd, POTENTIOMETER.S, LCD_1.GND, LASER_DIODE_3.-, LASER_DIODE1.-, LASER_DIODE_2.-
  N4: Part1.D9_PWM, ULTRASONIC_SENSOR.TRIG
  N5: Part1.D10_PWM/SS, ULTRASONIC_SENSOR.ECHO
  N6: Part1.D3_PWM, SERVO_MOTOR.pulse
  N7: Part1.D4, LASER_DIODE1.+
  N8: Part1.D5_PWM, LASER_DIODE_2.+
  N9: Part1.D6_PWM, LASER_DIODE_3.+
  N10: Part1.D7, BUZZER/ALARM.pin2
  VCC: Part1.5V, ACCELEROMETER.pin1, ULTRASONIC_SENSOR.VCC, SERVO_MOTOR.vcc, POTENTIOMETER.E, LCD_1.VCC

custom parts:
  GY-521 (MPU-6050): Placa GY-521 basada en conjunto de acelerómetro+giroscopios MPU-6050
  LCD screen 16x2 IIC: LCD screen with HD44780 controller enables showing text, symbols, value or anything else that comes from Croduino/Arduino. It is capable of showing 16 symbols in two lines and therefore can be used in many projects that need to send clearly visible and legible output information.. • Color of symbols: White • Backlight: Blue • Dimensions: 80 x 36 x 12 mm • Screen dimensions: 64.5 x 16 mm •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
