# Fritzing sketch Leveling System (saved by Fritzing 0.9.10b)

parts:
  Part1 = Arduino Uno (Rev3)
  LED = smd LED [color="Red (633nm)" package="0805 [SMD]"]
  BUZZER/ALARM = Piezo Speaker
  ACCELEROMETER = GY-521 (MPU-6050) [form="♀ (female)" package=THT]
  LASER_DIODE_1 = Electrolytic Capacitor [capacitance=1µF voltage=35V package="100 mil [THT, electrolytic]"]

nets:
  N1: Part1.A4/SDA, ACCELEROMETER.pin4, ACCELEROMETER.pin5
  N2: Part1.D8, LED.anode
  N3: Part1.GND, LED.cathode, ACCELEROMETER.pin2
  N4: Part1.A5/SCL, ACCELEROMETER.pin3
  N5: Part1.D6_PWM, LASER_DIODE_1.+
  N6: Part1.D7, BUZZER/ALARM.pin2
  N7: Part1.5V, ACCELEROMETER.pin1

custom parts:
  GY-521 (MPU-6050): Placa GY-521 basada en conjunto de acelerómetro+giroscopios MPU-6050
