# Fritzing sketch Main System (saved by Fritzing 0.9.10b)
breadboards: 1

parts:
  Part1 = Arduino Uno (Rev3)
  ULTRASONIC_SENSOR = HC-SR04 Ultrasonic Distance Sensor
  SERVO_MOTOR = Dagu DGServo 9g (Pan and tilt) [part_number=RS001B]
  POTENTIOMETER = POT [knob_status=50% power=0.5W package=pot_mammoth]
  LASER_DIODE1 = Electrolytic Capacitor [capacitance=1µF voltage=35V package="100 mil [THT, electrolytic]"]
  LASER_DIODE_2 = Electrolytic Capacitor [capacitance=1µF voltage=35V package="100 mil [THT, electrolytic]"]

nets:
  N1: Part1.A0, POTENTIOMETER.A
  N2: Part1.D9_PWM, ULTRASONIC_SENSOR.TRIG
  N3: Part1.D10_PWM/SS, ULTRASONIC_SENSOR.ECHO
  GND: Part1.GND, ULTRASONIC_SENSOR.GND, SERVO_MOTOR.gnd, POTENTIOMETER.S, LASER_DIODE_2.-
  N4: Part1.D3_PWM, SERVO_MOTOR.pulse
  N5: Part1.D4, LASER_DIODE1.+
  N6: Part1.D5_PWM, LASER_DIODE_2.+
  VCC: Part1.5V, ULTRASONIC_SENSOR.VCC, SERVO_MOTOR.vcc, POTENTIOMETER.E
